# Fritzing sketch sketch (saved by Fritzing 0.9.3b)

parts:
  Pro_Micro3 = Pro Micro
  Part1 = Bluetooth HC-05 Macho

nets:
  N1: Pro_Micro3.TX1, Part1.RXD
  N2: Pro_Micro3.RX0, Part1.TXD
  VCC: Pro_Micro3.VCC, Part1.VCC
  GND: Pro_Micro3.GND, Part1.GND

custom parts:
  Pro Micro: The SparkFun Pro Micro is a complete USB-based microcontoller development system, in a very small footprint, capable of implementing many types of projects. All programming can be done via the USB port.

// code stored in the sketch: fritzng_kod.ino
// include the library code:
#include <LiquidCrystal.h>

// initialize the library with the numbers of the interface pins
LiquidCrystal lcd(6, 7, 2, 3, 4, 5);
byte ss[8] = {
  0b01110,
  0b10001,
  0b10000,
  0b01110,
  0b00001,
  0b10101,
  0b01110,
  0b00100
};

int sensorValue = 0;
int outputValue = 0;
int sensorValue2 = 0;
int outputValue2 = 0;
int sensorPin = A0; 
int sensorPin2 = A1; 
float sonuc=0;
int islem = 0; 
int butondurum = 0; 
const int buton = 8;
void setup(){
  pinMode(buton, INPUT);
  lcd.begin(16, 2); /*sat?r sütun belirle, 2 sat?r?n 16 sütununu da kullanaca??m,
  tek sat?r kullanacaksan?z 1 yapabilirsiniz.*/
  
  lcd.clear();
  lcd.createChar(0, ss);
  lcd.write(byte(0));
  
  lcd.setCursor(0, 0);
  lcd.write("POTANSIYATOR"); 
} //end "setup()"

void loop(){
  lcd.clear();
  lcd.setCursor(0, 0);
  lcd.write("POTANSIYATOR"); 
  sensorValue = analogRead(sensorPin);
  outputValue  = map(sensorValue, 0, 1023, 0, 100);
  sensorValue2 = analogRead(sensorPin2);
  outputValue2  = map(sensorValue2, 0, 1023, 0, 20);
  lcd.setCursor(0, 1);
  lcd.print(outputValue);
  

  butondurum = digitalRead(buton);
  
  if (butondurum == HIGH) {  
    if(islem<4){islem++;}else{islem=0;}
  }
  if(islem==0){
   sonuc=(outputValue+outputValue2);
   lcd.print(" + ");
  }else if(islem==1){
    sonuc=(outputValue-outputValue2);
    lcd.print(" - ");
  }else if(islem==2){
    sonuc=(outputValue*outputValue2);
    lcd.print(" * ");
  }else if(islem==3){
    sonuc=(outputValue/outputValue2);
    lcd.print(" / ");
  }else if(islem==4){
   
    sonuc=pow(outputValue,outputValue2);
    lcd.print(" ^ ");
  }
  
  lcd.print(outputValue2);
  lcd.write(" = ");
   lcd.print(sonuc);
   delay(300);
} // end loop()
